# Fritzing sketch AR03_fnd (saved by Fritzing 0.9.3b)
breadboards: 1

parts:
  R1 = Resistor [tolerance=±5% resistance=330 package=THT]
  R2 = Resistor [tolerance=±5% resistance=330 package=THT]
  R3 = Resistor [tolerance=±5% resistance=330 package=THT]
  R4 = Resistor [tolerance=±5% resistance=330 package=THT]
  R5 = Resistor [tolerance=±5% resistance=330 package=THT]
  R6 = Resistor [tolerance=±5% resistance=330 package=THT]
  R7 = Resistor [tolerance=±5% resistance=330 package=THT]
  R8 = Resistor [tolerance=±5% resistance=330 package=THT]
  부품1 = Arduino Uno (Rev3)
  7_Segment1 = 7 Segment Display

nets:
  N1: R1.Pin_0, 부품1.D9_PWM
  N2: R1.Pin_1, 7_Segment1.Segment_DP
  N3: R2.Pin_0, 7_Segment1.Segment_B
  N4: R2.Pin_1, 부품1.D3_PWM
  N5: R3.Pin_0, 7_Segment1.Segment_F
  N6: R3.Pin_1, 부품1.D8
  N7: R4.Pin_0, 부품1.D4
  N8: R4.Pin_1, 7_Segment1.Segment_C
  N9: R5.Pin_0, 부품1.D5_PWM
  N10: R5.Pin_1, 7_Segment1.Segment_D
  N11: R6.Pin_0, 7_Segment1.Segment_G
  N12: R6.Pin_1, 부품1.D7
  N13: R7.Pin_0, 7_Segment1.Segment_A
  N14: R7.Pin_1, 부품1.D2
  N15: R8.Pin_0, 부품1.D6_PWM
  N16: R8.Pin_1, 7_Segment1.Segment_E
  N17: 부품1.GND, 7_Segment1.common_anode
