# Fritzing sketch AR03_4digit (saved by Fritzing 0.9.3b)
breadboards: 1

parts:
  R1 = Resistor [tolerance=±5% resistance=330 package=THT]
  부품1 = Arduino Uno (Rev3)
  R2 = Resistor [tolerance=±5% resistance=330 package=THT]
  R3 = Resistor [tolerance=±5% resistance=330 package=THT]
  R4 = Resistor [tolerance=±5% resistance=330 package=THT]
  R5 = Resistor [tolerance=±5% resistance=330 package=THT]
  R6 = Resistor [tolerance=±5% resistance=330 package=THT]
  R7 = Resistor [tolerance=±5% resistance=330 package=THT]
  R8 = Resistor [tolerance=±5% resistance=330 package=THT]
  U5 = 7-SEGMENT-4DIGIT [package=7-segment-4digit-5641]

nets:
  N1: R1.Pin_0, 부품1.D4, U5.C
  N2: 부품1.D8, R2.Pin_0, U5.G
  N3: 부품1.D9_PWM, R3.Pin_1, U5.DP
  N4: 부품1.D10_PWM/SS, U5.DIG1
  N5: 부품1.D11_PWM/MOSI, U5.DIG2
  N6: 부품1.D12/MISO, U5.DIG3
  N7: 부품1.D13/SCK, U5.DIG4
  N8: 부품1.D2, R7.Pin_0
  N9: 부품1.D3_PWM, R8.Pin_1
  N10: 부품1.D5_PWM, R4.Pin_0
  N11: 부품1.D6_PWM, R5.Pin_0
  N12: 부품1.D7, R6.Pin_0
  N13: R4.Pin_1, U5.D
  N14: R5.Pin_1, U5.E
  N15: R6.Pin_1, U5.F
  N16: R7.Pin_1, U5.A
  N17: R8.Pin_0, U5.B

custom parts:
  7-SEGMENT-4DIGIT: if you need make parts, send me e-mail and write. Price 1 part=0.9 WMZ (http://www.wmtransfer.com/) ~ 0.9 Euro
